// Digital circuit homework 1.dig as structural Verilog
module homework_1 (
  input  A,
  input  B,
  input  C_in,
  input  [3:0] A_2,
  input  [3:0] B_2,
  input  Carry_in,
  input  A0,
  input  A1,
  input  B0,
  input  B1,
  output S,
  output C_out,
  output [3:0] Sum,
  output Carry_out,
  output P0,
  output P1,
  output P2,
  output P3
);

  wire add_2_c_o, add_3_c_o, add_4_c_o, and_1_out, and_3_out, and_4_out, and_5_out, and_6_out, and_7_out,
       xor_1_out;

  xor xor_1 (xor_1_out, A, B);
  and and_1 (and_1_out, A, B);
  Add add_1 (.a(A_2[3]), .b(B_2[3]), .c_i(add_2_c_o), .s(Sum[3]), .c_o(Carry_out));
  and and_2 (P0, A0, B0);
  and and_3 (and_3_out, A1, B1);
  and and_4 (and_4_out, A0, B1);
  and and_5 (and_5_out, A1, B0);
  and and_6 (and_6_out, xor_1_out, C_in);
  Add add_2 (.a(A_2[2]), .b(B_2[2]), .c_i(add_3_c_o), .s(Sum[2]), .c_o(add_2_c_o));
  xor xor_2 (S, xor_1_out, C_in);
  or or_1 (C_out, and_6_out, and_1_out);
  Add add_3 (.a(A_2[1]), .b(B_2[1]), .c_i(add_4_c_o), .s(Sum[1]), .c_o(add_3_c_o));
  xor xor_3 (P1, and_4_out, and_5_out);
  and and_7 (and_7_out, and_4_out, and_5_out);
  Add add_4 (.a(A_2[0]), .b(B_2[0]), .c_i(Carry_in), .s(Sum[0]), .c_o(add_4_c_o));
  xor xor_4 (P2, and_3_out, and_7_out);
  and and_8 (P3, and_3_out, and_7_out);

  // Notes on the sheet:
  //   Question 6:
  //   Question 4:
  //   Question 5:
endmodule
